// Logisim project lab08.circ as structural Verilog: 4 circuits, main circuit main
module main (
  input  [3:0] ALUOperation,
  input  [7:0] A,
  input  [7:0] B,
  output Zero,
  output [7:0] Result,
  output Overflow
);

  _8_bit_ALU u_8_bit_alu_1 (.A(A), .B(B), .Operation(ALUOperation), .Zero(Zero), .Result(Result), .Overflow(Overflow));
endmodule

module _1_bit_ALU (
  input  Ainvert,
  input  Binvert,
  input  CarryIn,
  input  [1:0] Operation,
  input  a,
  input  b,
  input  less,
  output Result,
  output Set,
  output CarryOut
);

  wire and_1_out, multiplexer_1_out, multiplexer_2_out, not_1_out, not_2_out, or_1_out;

  not not_1 (not_1_out, a);
  not not_2 (not_2_out, b);
  Multiplexer #(.enable("false")) multiplexer_1 (.in0(a), .in1(not_1_out), .out(multiplexer_1_out), .sel(Ainvert));
  Multiplexer #(.enable("false")) multiplexer_2 (.in0(b), .in1(not_2_out), .out(multiplexer_2_out), .sel(Binvert));
  and and_1 (and_1_out, multiplexer_1_out, multiplexer_2_out);
  or or_1 (or_1_out, multiplexer_1_out, multiplexer_2_out);
  Adder #(.width(1)) adder_1 (.a(multiplexer_1_out), .b(multiplexer_2_out), .out(Set), .cin(CarryIn), .cout(CarryOut));
  Multiplexer #(.select(2), .enable("false")) multiplexer_3 (
    .in0(and_1_out), .in1(or_1_out), .in2(Set), .in3(less), .out(Result), .sel(Operation));
endmodule

module _8_bit_ALU (
  input  [7:0] A,
  input  [3:0] Operation,
  input  [7:0] B,
  output Zero,
  output [7:0] Result,
  output Overflow
);

  wire n1_bit_alu_1_set, n1_bit_alu_2_carryout, n1_bit_alu_3_carryout, n1_bit_alu_4_carryout,
       n1_bit_alu_5_carryout, n1_bit_alu_6_carryout, n1_bit_alu_7_carryout, n1_bit_alu_8_carryout, xor_1_out;

  _1_bit_ALU u_1_bit_alu_1 (
    .a(A[7]), .b(B[7]), .less(1'b0), .Ainvert(Operation[3]), .Binvert(Operation[2]),
    .CarryIn(n1_bit_alu_4_carryout), .Operation(Operation[1:0]), .Result(Result[7]), .Set(n1_bit_alu_1_set));  // open: CarryOut
  _1_bit_ALU u_1_bit_alu_2 (
    .a(A[4]), .b(B[4]), .less(1'b0), .Ainvert(Operation[3]), .Binvert(Operation[2]),
    .CarryIn(n1_bit_alu_7_carryout), .Operation(Operation[1:0]), .CarryOut(n1_bit_alu_2_carryout),
    .Result(Result[4]));  // open: Set
  _1_bit_ALU u_1_bit_alu_3 (
    .a(A[5]), .b(B[5]), .less(1'b0), .Ainvert(Operation[3]), .Binvert(Operation[2]),
    .CarryIn(n1_bit_alu_2_carryout), .Operation(Operation[1:0]), .CarryOut(n1_bit_alu_3_carryout),
    .Result(Result[5]));  // open: Set
  _1_bit_ALU u_1_bit_alu_4 (
    .a(A[6]), .b(B[6]), .less(1'b0), .Ainvert(Operation[3]), .Binvert(Operation[2]),
    .CarryIn(n1_bit_alu_3_carryout), .Operation(Operation[1:0]), .CarryOut(n1_bit_alu_4_carryout),
    .Result(Result[6]));  // open: Set
  Overflow overflow_1 (.A(B[7]), .B(A[7]), .MSB(n1_bit_alu_1_set), .Bnegate(Operation[2]), .Overflow(Overflow));
  _1_bit_ALU u_1_bit_alu_5 (
    .a(A[1]), .b(B[1]), .less(1'b0), .Ainvert(Operation[3]), .Binvert(Operation[2]),
    .CarryIn(n1_bit_alu_8_carryout), .Operation(Operation[1:0]), .CarryOut(n1_bit_alu_5_carryout),
    .Result(Result[1]));  // open: Set
  _1_bit_ALU u_1_bit_alu_6 (
    .a(A[2]), .b(B[2]), .less(1'b0), .Ainvert(Operation[3]), .Binvert(Operation[2]),
    .CarryIn(n1_bit_alu_5_carryout), .Operation(Operation[1:0]), .CarryOut(n1_bit_alu_6_carryout),
    .Result(Result[2]));  // open: Set
  _1_bit_ALU u_1_bit_alu_7 (
    .a(A[3]), .b(B[3]), .less(1'b0), .Ainvert(Operation[3]), .Binvert(Operation[2]),
    .CarryIn(n1_bit_alu_6_carryout), .Operation(Operation[1:0]), .CarryOut(n1_bit_alu_7_carryout),
    .Result(Result[3]));  // open: Set
  xor xor_1 (xor_1_out, n1_bit_alu_1_set, Overflow);
  _1_bit_ALU u_1_bit_alu_8 (
    .a(A[0]), .b(B[0]), .less(xor_1_out), .Ainvert(Operation[3]), .Binvert(Operation[2]),
    .CarryIn(Operation[2]), .Operation(Operation[1:0]), .CarryOut(n1_bit_alu_8_carryout), .Result(Result[0]));  // open: Set
  nor nor_1 (Zero, Result[0], Result[1], Result[2], Result[3], Result[4], Result[5], Result[6], Result[7]);
endmodule

module Overflow (
  input  A,
  input  B,
  input  MSB,
  input  Bnegate,
  output Overflow
);

  wire and_1_out, and_2_out, and_3_out, and_4_out, not_1_out, not_2_out, not_3_out, or_1_out, or_2_out;

  not not_1 (not_1_out, A);
  not not_2 (not_2_out, B);
  not not_3 (not_3_out, MSB);
  and and_1 (and_1_out, not_3_out, B, A);
  and and_2 (and_2_out, MSB, not_2_out, not_1_out);
  and and_3 (and_3_out, MSB, B, not_1_out);
  and and_4 (and_4_out, not_3_out, not_2_out, A);
  or or_1 (or_1_out, and_1_out, and_2_out);
  or or_2 (or_2_out, and_3_out, and_4_out);
  Multiplexer #(.enable("false")) multiplexer_1 (.in0(or_1_out), .in1(or_2_out), .out(Overflow), .sel(Bnegate));
endmodule
