// Logisim project lab10.circ as structural Verilog: 4 circuits, main circuit main
module main (
);

  wire decoder_1_dstmux;
  wire [1:0] decoder_1_alu;
  wire [3:0] fields_1_opcode;
  wire [7:0] A_q, adder_1_out, alu_1_result, B_q, fields_1_imm, multiplexer_1_out, PC_q;

  Adder adder_1 (.a(PC_q), .out(adder_1_out));  // open: b, cin, cout
  Register PC (.D(adder_1_out), .en(1'b1), .Q(PC_q));  // open: clk, clr
  ROM #(.dataWidth(16)) rom_1 (.addr(PC_q), .sel(1'b1));  // open: data
  ALU alu_1 (.A(A_q), .B(B_q), .Operation(decoder_1_alu), .Result(alu_1_result));  // open: CarryIn, c1, c2
  Register A (.D(multiplexer_1_out), .Q(A_q));  // open: en, clk, clr
  Register B (.D(multiplexer_1_out), .Q(B_q));  // open: en, clk, clr
  Multiplexer #(.width(8)) multiplexer_1 (
    .in0(alu_1_result), .in1(fields_1_imm), .out(multiplexer_1_out));  // open: sel, en
  Fields fields_1 (.OpCode(fields_1_opcode), .Imm(fields_1_imm));  // open: Input, register
  Decoder decoder_1 (.OpCode(fields_1_opcode), .ALU(decoder_1_alu), .DstMux(decoder_1_dstmux));
endmodule

module ALU (
  input  CarryIn,
  input  [7:0] A,
  input  [1:0] Operation,
  input  [7:0] B,
  output c1,
  output c2,
  output [7:0] Result
);

  wire [7:0] adder_1_out, and_1_out, or_1_out, subtractor_1_out;

  Adder adder_1 (.a(A), .b(B), .out(adder_1_out), .cin(CarryIn), .cout(c1));
  Subtractor subtractor_1 (.a(A), .b(B), .out(subtractor_1_out), .bout(c2));  // open: bin
  assign and_1_out = A & B;  // AND_Gate and_1, 8 bits wide
  assign or_1_out = A | B;  // OR_Gate or_1, 8 bits wide
  Multiplexer #(.select(2), .width(8), .enable("false")) multiplexer_1 (
    .in0(adder_1_out), .in1(subtractor_1_out), .in2(and_1_out), .in3(or_1_out), .out(Result), .sel(Operation));
endmodule

module Fields (
  input  [15:0] Input,
  output [3:0] OpCode,
  output register,
  output [7:0] Imm
);


  assign Imm = Input[15:8];
  assign OpCode = Input[3:0];
  assign register = Input[4];
endmodule

module Decoder (
  input  [3:0] OpCode,
  output [1:0] ALU,
  output DstMux
);

  wire not_2_out, not_3_out;

  not not_1 (ALU[1], OpCode[1]);
  not not_2 (not_2_out, OpCode[2]);
  and and_1 (DstMux, not_2_out, not_3_out);
  not not_3 (not_3_out, OpCode[1]);

  assign ALU[0] = OpCode[0];
endmodule
